// Logisim project Contador 0-23 (Horas).circ as structural Verilog: 1 circuit, main circuit main
module main (
);

  wire and_1_out, and_2_out, and_3_out, and_4_out, clock_1_out, main_1_q0, main_1_q1, main_1_q2, main_1_q3,
       main_2_b, main_2_bl, main_2_br, main_2_m, main_2_t, main_2_tl, main_2_tr, main_3_q0, main_3_q1,
       main_3_q2, main_3_q3, main_4_b, main_4_bl, main_4_br, main_4_m, main_4_t, main_4_tl, main_4_tr,
       or_1_out;

  _0_10_Flip_Flop_main main_1 (
    .Clock(and_1_out), .Reset(and_3_out), .Q3(main_1_q3), .Q2(main_1_q2), .Q1(main_1_q1), .Q0(main_1_q0));  // open: Set
  and and_1 (and_1_out, main_3_q3, ~main_3_q2, main_3_q1, ~main_3_q0);  // AND_Gate
  and and_2 (and_2_out, ~main_1_q3, ~main_1_q2, main_1_q1, ~main_1_q0);  // AND_Gate
  \Decodificador_Binário_para_Algorismo_Decimal_main  main_2 (
    .E8(main_1_q3), .E4(main_1_q2), .E2(main_1_q1), .E1(main_1_q0), .M(main_2_m), .TL(main_2_tl),
    .T(main_2_t), .TR(main_2_tr), .BL(main_2_bl), .B(main_2_b), .BR(main_2_br));
  and and_3 (and_3_out, and_2_out, and_4_out);
  _7_Segment_Display u_7_segment_display_1 (
    .g(main_2_m), .f(main_2_tl), .a(main_2_t), .b(main_2_tr), .e(main_2_bl), .d(main_2_b), .c(main_2_br));  // open: dp
  Clock clock_1 (.out(clock_1_out));
  or or_1 (or_1_out, and_1_out, and_3_out);
  _0_10_Flip_Flop_main main_3 (
    .Clock(clock_1_out), .Reset(or_1_out), .Q3(main_3_q3), .Q2(main_3_q2), .Q1(main_3_q1), .Q0(main_3_q0));  // open: Set
  and and_4 (and_4_out, ~main_3_q3, main_3_q2, ~main_3_q1, ~main_3_q0);  // AND_Gate
  \Decodificador_Binário_para_Algorismo_Decimal_main  main_4 (
    .E8(main_3_q3), .E4(main_3_q2), .E2(main_3_q1), .E1(main_3_q0), .M(main_4_m), .TL(main_4_tl),
    .T(main_4_t), .TR(main_4_tr), .BL(main_4_bl), .B(main_4_b), .BR(main_4_br));
  _7_Segment_Display u_7_segment_display_2 (
    .g(main_4_m), .f(main_4_tl), .a(main_4_t), .b(main_4_tr), .e(main_4_bl), .d(main_4_b), .c(main_4_br));  // open: dp
endmodule
