// Logisim project Codificador Algarismo Decimal.circ as structural Verilog: 1 circuit, main circuit main
module main (
  input  E0,
  input  E1,
  input  E2,
  input  E3,
  input  E4,
  input  E5,
  input  E6,
  input  E7,
  input  E8,
  input  E9,
  output S8,
  output S4,
  output S2,
  output S1
);

  wire and_1_out, and_2_out, and_3_out, and_4_out, and_5_out, and_6_out, and_7_out, and_8_out, and_9_out,
       and_10_out, and_11_out, and_12_out, and_13_out, and_14_out, and_15_out, not_1_out, not_2_out,
       not_3_out, not_4_out, not_5_out, not_6_out, not_7_out, not_8_out, not_9_out, not_10_out, not_11_out,
       not_12_out, not_13_out, not_14_out, not_15_out, not_16_out, not_17_out, not_18_out, not_19_out,
       not_20_out, not_21_out, not_22_out, not_23_out, not_24_out, not_25_out, not_26_out, not_27_out,
       not_28_out, not_29_out, not_30_out, not_31_out, not_32_out, not_33_out, not_34_out, not_35_out,
       not_36_out, not_37_out, not_38_out, not_39_out, not_40_out, not_41_out, not_42_out, not_43_out,
       not_44_out, not_45_out, not_46_out, not_47_out, not_48_out, not_49_out, not_50_out, not_51_out,
       not_52_out, not_53_out, not_54_out, not_55_out, not_56_out, not_57_out, not_58_out, not_59_out,
       not_60_out, not_61_out, not_62_out, not_63_out, not_64_out, not_65_out, not_66_out, not_67_out,
       not_68_out, not_69_out, not_70_out, not_71_out, not_72_out, not_73_out, not_74_out, not_75_out,
       not_76_out, not_77_out, not_78_out, not_79_out, not_80_out, not_81_out, not_82_out, not_83_out,
       not_84_out, not_85_out, not_86_out, not_87_out, not_88_out, not_89_out;

  not not_1 (not_1_out, E0);
  not not_2 (not_2_out, E2);
  not not_3 (not_3_out, E4);
  not not_4 (not_4_out, E6);
  not not_5 (not_5_out, E8);
  not not_6 (not_6_out, E0);
  not not_7 (not_7_out, E2);
  not not_8 (not_8_out, E4);
  not not_9 (not_9_out, E6);
  not not_10 (not_10_out, E8);
  not not_11 (not_11_out, E0);
  not not_12 (not_12_out, E2);
  not not_13 (not_13_out, E4);
  not not_14 (not_14_out, E6);
  not not_15 (not_15_out, E8);
  not not_16 (not_16_out, E0);
  not not_17 (not_17_out, E2);
  not not_18 (not_18_out, E4);
  not not_19 (not_19_out, E6);
  not not_20 (not_20_out, E8);
  not not_21 (not_21_out, E0);
  not not_22 (not_22_out, E2);
  not not_23 (not_23_out, E4);
  not not_24 (not_24_out, E6);
  not not_25 (not_25_out, E8);
  not not_26 (not_26_out, E0);
  not not_27 (not_27_out, E1);
  not not_28 (not_28_out, E4);
  not not_29 (not_29_out, E5);
  not not_30 (not_30_out, E8);
  not not_31 (not_31_out, E9);
  not not_32 (not_32_out, E0);
  not not_33 (not_33_out, E1);
  not not_34 (not_34_out, E4);
  not not_35 (not_35_out, E5);
  not not_36 (not_36_out, E8);
  not not_37 (not_37_out, E9);
  not not_38 (not_38_out, E0);
  not not_39 (not_39_out, E1);
  not not_40 (not_40_out, E4);
  not not_41 (not_41_out, E5);
  not not_42 (not_42_out, E8);
  not not_43 (not_43_out, E9);
  not not_44 (not_44_out, E0);
  not not_45 (not_45_out, E1);
  not not_46 (not_46_out, E4);
  not not_47 (not_47_out, E5);
  not not_48 (not_48_out, E8);
  not not_49 (not_49_out, E9);
  not not_50 (not_50_out, E0);
  not not_51 (not_51_out, E1);
  not not_52 (not_52_out, E2);
  not not_53 (not_53_out, E3);
  not not_54 (not_54_out, E8);
  not not_55 (not_55_out, E9);
  not not_56 (not_56_out, E0);
  not not_57 (not_57_out, E1);
  not not_58 (not_58_out, E2);
  not not_59 (not_59_out, E3);
  not not_60 (not_60_out, E8);
  not not_61 (not_61_out, E9);
  not not_62 (not_62_out, E0);
  not not_63 (not_63_out, E1);
  not not_64 (not_64_out, E2);
  not not_65 (not_65_out, E3);
  not not_66 (not_66_out, E8);
  not not_67 (not_67_out, E9);
  not not_68 (not_68_out, E0);
  not not_69 (not_69_out, E1);
  not not_70 (not_70_out, E2);
  not not_71 (not_71_out, E3);
  not not_72 (not_72_out, E8);
  not not_73 (not_73_out, E9);
  not not_74 (not_74_out, E0);
  not not_75 (not_75_out, E1);
  not not_76 (not_76_out, E2);
  not not_77 (not_77_out, E3);
  not not_78 (not_78_out, E4);
  not not_79 (not_79_out, E5);
  not not_80 (not_80_out, E6);
  not not_81 (not_81_out, E7);
  not not_82 (not_82_out, E0);
  not not_83 (not_83_out, E1);
  not not_84 (not_84_out, E2);
  not not_85 (not_85_out, E3);
  not not_86 (not_86_out, E4);
  not not_87 (not_87_out, E5);
  not not_88 (not_88_out, E6);
  not not_89 (not_89_out, E7);
  and and_1 (and_1_out, not_1_out, not_2_out, not_3_out, not_4_out, not_5_out, E9);
  and and_2 (and_2_out, not_6_out, not_7_out, not_8_out, not_9_out, E7, not_10_out);
  and and_3 (and_3_out, not_11_out, not_12_out, not_13_out, E5, not_14_out, not_15_out);
  and and_4 (and_4_out, not_16_out, not_17_out, E3, not_18_out, not_19_out, not_20_out);
  and and_5 (and_5_out, not_21_out, E1, not_22_out, not_23_out, not_24_out, not_25_out);
  and and_6 (and_6_out, not_26_out, not_27_out, not_28_out, not_29_out, E7, not_30_out, not_31_out);
  and and_7 (and_7_out, not_32_out, not_33_out, not_34_out, not_35_out, E6, not_36_out, not_37_out);
  and and_8 (and_8_out, not_38_out, not_39_out, E3, not_40_out, not_41_out, not_42_out, not_43_out);
  and and_9 (and_9_out, not_44_out, not_45_out, E2, not_46_out, not_47_out, not_48_out, not_49_out);
  and and_10 (and_10_out, not_50_out, not_51_out, not_52_out, not_53_out, E7, not_54_out, not_55_out);
  and and_11 (and_11_out, not_56_out, not_57_out, not_58_out, not_59_out, E6, not_60_out, not_61_out);
  and and_12 (and_12_out, not_62_out, not_63_out, not_64_out, not_65_out, E5, not_66_out, not_67_out);
  and and_13 (and_13_out, not_68_out, not_69_out, not_70_out, not_71_out, E4, not_72_out, not_73_out);
  and and_14 (and_14_out, not_74_out, not_75_out, not_76_out, not_77_out, not_78_out, not_79_out, not_80_out, not_81_out, E9);
  and and_15 (and_15_out, not_82_out, not_83_out, not_84_out, not_85_out, not_86_out, not_87_out, not_88_out, not_89_out, E8);
  or or_1 (S1, and_1_out, and_2_out, and_3_out, and_4_out, and_5_out);
  or or_2 (S2, and_6_out, and_7_out, and_8_out, and_9_out);
  or or_3 (S4, and_10_out, and_11_out, and_12_out, and_13_out);
  or or_4 (S8, and_14_out, and_15_out);
endmodule
