// Logisim project Complemento de 2  4 bits.circ as structural Verilog: 1 circuit, main circuit main
module main (
  input  ES,
  input  E4,
  input  E2,
  input  E1,
  output SS,
  output S4,
  output S2,
  output S1
);

  wire and_1_out, and_2_out, and_3_out, and_4_out, and_5_out, and_6_out, and_7_out, and_8_out, and_9_out,
       and_10_out, not_1_out, not_2_out, not_3_out, not_4_out, not_5_out, not_6_out, not_7_out, not_8_out,
       not_9_out, not_10_out, not_11_out;

  not not_1 (not_1_out, E4);
  not not_2 (not_2_out, E2);
  not not_3 (not_3_out, E1);
  not not_4 (not_4_out, ES);
  and and_1 (and_1_out, not_4_out, E4);
  and and_2 (and_2_out, E4, not_5_out, not_6_out);
  not not_5 (not_5_out, E2);
  not not_6 (not_6_out, E1);
  and and_3 (and_3_out, ES, not_7_out, E1);
  not not_7 (not_7_out, E4);
  not not_8 (not_8_out, E4);
  and and_4 (and_4_out, ES, not_8_out, E2);
  not not_9 (not_9_out, ES);
  and and_5 (and_5_out, not_9_out, E2);
  and and_6 (and_6_out, E2, not_10_out);
  not not_10 (not_10_out, E1);
  and and_7 (and_7_out, ES, not_11_out, E1);
  not not_11 (not_11_out, E2);
  and and_8 (and_8_out, E2, E1);
  and and_9 (and_9_out, E4, E1);
  and and_10 (and_10_out, ES, E1);
  and and_11 (SS, ES, not_1_out, not_2_out, not_3_out);
  or or_1 (S4, and_1_out, and_2_out, and_3_out, and_4_out);
  or or_2 (S2, and_5_out, and_6_out, and_7_out);
  or or_3 (S1, and_8_out, and_9_out, and_10_out);
endmodule
