// Logisim project DEMUX 1-2.circ as structural Verilog: 1 circuit, main circuit main
module main (
  input  E,
  input  Ctrl,
  output S0,
  output S1
);

  wire not_1_out;

  not not_1 (not_1_out, Ctrl);
  and and_1 (S0, not_1_out, E);
  and and_2 (S1, Ctrl, E);
endmodule
