// Logisim project Decodificador Binário para Algorismo Decimal.circ as structural Verilog: 1 circuit, main circuit main
module main (
  input  E8,
  input  E4,
  input  E2,
  input  E1,
  output M,
  output TL,
  output T,
  output TR,
  output BL,
  output B,
  output BR
);

  wire and_1_out, and_2_out, and_3_out, and_4_out, and_5_out, and_6_out, and_7_out, and_8_out, and_9_out,
       and_10_out, and_11_out, and_12_out, and_13_out, and_14_out, and_15_out, and_16_out, not_1_out,
       not_2_out, not_3_out, not_4_out, not_5_out, not_6_out, not_7_out, not_8_out, not_9_out, not_10_out,
       not_11_out, not_12_out, not_13_out, not_14_out, not_15_out, not_16_out, not_17_out, not_18_out,
       not_19_out, not_20_out, not_21_out, not_22_out;

  not not_1 (not_1_out, E4);
  and and_1 (and_1_out, not_1_out, E2);
  and and_2 (and_2_out, E4, not_2_out);
  not not_2 (not_2_out, E2);
  and and_3 (and_3_out, E4, not_3_out);
  not not_3 (not_3_out, E1);
  not not_4 (not_4_out, E2);
  and and_4 (and_4_out, not_4_out, not_5_out);
  not not_5 (not_5_out, E1);
  and and_5 (and_5_out, E4, not_6_out);
  not not_6 (not_6_out, E2);
  and and_6 (and_6_out, E4, not_7_out);
  not not_7 (not_7_out, E1);
  not not_8 (not_8_out, E4);
  and and_7 (and_7_out, not_8_out, not_9_out);
  not not_9 (not_9_out, E1);
  and and_8 (and_8_out, E4, E1);
  not not_10 (not_10_out, E4);
  not not_11 (not_11_out, E2);
  and and_9 (and_9_out, not_11_out, not_12_out);
  not not_12 (not_12_out, E1);
  and and_10 (and_10_out, E2, E1);
  not not_13 (not_13_out, E4);
  and and_11 (and_11_out, not_13_out, not_14_out);
  not not_14 (not_14_out, E1);
  and and_12 (and_12_out, E2, not_15_out);
  not not_15 (not_15_out, E1);
  not not_16 (not_16_out, E4);
  and and_13 (and_13_out, not_16_out, not_17_out);
  not not_17 (not_17_out, E1);
  not not_18 (not_18_out, E8);
  not not_19 (not_19_out, E4);
  and and_14 (and_14_out, not_18_out, not_19_out, E2);
  and and_15 (and_15_out, E2, not_20_out);
  not not_20 (not_20_out, E1);
  and and_16 (and_16_out, E4, not_21_out, E1);
  not not_21 (not_21_out, E2);
  not not_22 (not_22_out, E2);
  or or_1 (BR, not_22_out, E1, E4);
  or or_2 (M, and_1_out, and_2_out, and_3_out, E8);
  or or_3 (TL, and_4_out, and_5_out, and_6_out, E8);
  or or_4 (T, and_7_out, E2, and_8_out, E8);
  or or_5 (TR, not_10_out, and_9_out, and_10_out);
  or or_6 (BL, and_11_out, and_12_out);
  or or_7 (B, and_13_out, and_14_out, and_15_out, and_16_out);
  _7_Segment_Display u_7_segment_display_1 (.g(M), .f(TL), .a(T), .b(TR), .e(BL), .d(B), .c(BR));  // open: dp
endmodule
