// Logisim project DEMUX 1-4.circ as structural Verilog: 1 circuit, main circuit main
module main (
  input  E,
  input  Ctrl1,
  input  Ctrl2,
  output S0,
  output S1,
  output S2,
  output S3
);

  wire not_1_out, not_2_out;

  not not_1 (not_1_out, Ctrl1);
  not not_2 (not_2_out, Ctrl2);
  and and_1 (S0, not_2_out, not_1_out, E);
  and and_2 (S1, Ctrl2, not_1_out, E);
  and and_3 (S2, not_2_out, Ctrl1, E);
  and and_4 (S3, Ctrl2, Ctrl1, E);
endmodule
