// Logisim project MUX 2-1.circ as structural Verilog: 1 circuit, main circuit main
module main (
  input  E0,
  input  E1,
  input  Ctrl1,
  output S
);

  wire and_1_out, and_2_out, not_1_out;

  not not_1 (not_1_out, Ctrl1);
  and and_1 (and_1_out, E1, Ctrl1);
  and and_2 (and_2_out, E0, not_1_out);
  or or_1 (S, and_1_out, and_2_out);
endmodule
