// Logisim project MUX 4-1.circ as structural Verilog: 1 circuit, main circuit main
module main (
  input  E0,
  input  E1,
  input  E2,
  input  E3,
  input  Ctrl1,
  input  Ctrl2,
  output out_7
);

  wire and_1_out, and_2_out, and_3_out, and_4_out, not_1_out, not_2_out;

  not not_1 (not_1_out, Ctrl1);
  not not_2 (not_2_out, Ctrl2);
  and and_1 (and_1_out, not_2_out, not_1_out, E0);
  and and_2 (and_2_out, not_1_out, Ctrl2, E1);
  and and_3 (and_3_out, not_2_out, Ctrl1, E2);
  and and_4 (and_4_out, Ctrl2, Ctrl1, E3);
  or or_1 (out_7, and_1_out, and_2_out, and_3_out, and_4_out);
endmodule
