// Logisim project 0-10 Flip Flop.circ as structural Verilog: 1 circuit, main circuit main
module main (
  input  Clock,
  input  Set,
  input  Reset,
  output Q3,
  output Q2,
  output Q1,
  output Q0
);

  wire and_1_out, and_2_out, j_k_ff_1_qn, j_k_ff_3_qn, main_1_b, main_1_bl, main_1_br, main_1_m, main_1_t,
       main_1_tl, main_1_tr, or_1_out, or_2_out;

  and and_1 (and_1_out, Q2, Q1, Q0);
  J_K_Flip_Flop j_k_ff_1 (
    .J(and_1_out), .clk(Clock), .K(Q1), .Q(Q3), .Qn(j_k_ff_1_qn), .preset(Set), .reset(Reset));  // open: en
  and and_2 (and_2_out, Q1, Q0);
  J_K_Flip_Flop j_k_ff_2 (
    .J(and_2_out), .clk(Clock), .K(and_2_out), .Q(Q2), .preset(Set), .reset(Reset));  // open: Qn, en
  or or_1 (or_1_out, Q3, Q0);
  J_K_Flip_Flop j_k_ff_3 (
    .J(Q0), .clk(Clock), .K(or_1_out), .Q(Q1), .Qn(j_k_ff_3_qn), .preset(Set), .reset(Reset));  // open: en
  or or_2 (or_2_out, j_k_ff_3_qn, j_k_ff_1_qn);
  J_K_Flip_Flop j_k_ff_4 (.J(or_2_out), .clk(Clock), .K(1'b1), .Q(Q0), .preset(Set), .reset(Reset));  // open: Qn, en
  \Decodificador_Binário_para_Algorismo_Decimal_main  main_1 (
    .E8(Q3), .E4(Q2), .E2(Q1), .E1(Q0), .M(main_1_m), .TL(main_1_tl), .T(main_1_t), .TR(main_1_tr),
    .BL(main_1_bl), .B(main_1_b), .BR(main_1_br));
  _7_Segment_Display u_7_segment_display_1 (
    .g(main_1_m), .f(main_1_tl), .a(main_1_t), .b(main_1_tr), .e(main_1_bl), .d(main_1_b), .c(main_1_br));  // open: dp

  // Notes on the sheet:
  //   Q0Q1Q2
  //   Q1
  //   Q0Q1
  //   Q0
  //   Q0+Q3
  //   Q0~ + Q1 + Q2~
endmodule
