// Logisim project Somador Binário Completo 4 bits.circ as structural Verilog: 1 circuit, main circuit main
module main (
  input  B0,
  input  A0,
  input  B1,
  input  A1,
  input  B2,
  input  A2,
  input  B3,
  input  A3
);

  wire main_1_p4, main_1_p5, main_2_p4, main_2_p5, main_3_p4, main_3_p5, main_4_p4, main_5_b, main_5_bl,
       main_5_br, main_5_m, main_5_t, main_5_tl, main_5_tr;

  // Somador_Binário_completo_main main_1: pin names not known; wires that end beside it: A0, B0, 1'b0, main_1_p4, main_1_p5
  // Somador_Binário_completo_main main_2: pin names not known; wires that end beside it: A1, B1, main_1_p5, main_2_p4, main_2_p5
  // Somador_Binário_completo_main main_3: pin names not known; wires that end beside it: A2, B2, main_2_p5, main_3_p4, main_3_p5
  // Somador_Binário_completo_main main_4: pin names not known; wires that end beside it: A3, B3, main_3_p5, main_4_p4
  \Decodificador_Binário_para_Algorismo_Decimal_main  main_5 (
    .E8(main_4_p4), .E4(main_3_p4), .E2(main_2_p4), .E1(main_1_p4), .M(main_5_m), .TL(main_5_tl),
    .T(main_5_t), .TR(main_5_tr), .BL(main_5_bl), .B(main_5_b), .BR(main_5_br));
  _7_Segment_Display u_7_segment_display_1 (
    .g(main_5_m), .f(main_5_tl), .a(main_5_t), .b(main_5_tr), .e(main_5_bl), .d(main_5_b), .c(main_5_br));  // open: dp
endmodule
