// Logisim project Subtrator completo 4 bits (errado).circ as structural Verilog: 1 circuit, main circuit main
module main (
  input  A0,
  input  B0,
  input  A1,
  input  B1,
  input  A2,
  input  B2,
  input  A3,
  input  B3
);

  wire main_1_s, main_2_bout, main_2_s, main_3_bout, main_3_s, main_4_bout, main_4_s, main_5_b, main_5_bl,
       main_5_br, main_5_m, main_5_t, main_5_tl, main_5_tr;

  Subtrator_incompleto_1bit_main main_1 (.A(A0), .B(B0), .Cin(main_2_bout), .S(main_1_s));  // open: Bout
  Subtrator_incompleto_1bit_main main_2 (.A(A1), .B(B1), .Cin(main_3_bout), .S(main_2_s), .Bout(main_2_bout));
  Subtrator_incompleto_1bit_main main_3 (.A(A2), .B(B2), .Cin(main_4_bout), .S(main_3_s), .Bout(main_3_bout));
  Subtrator_incompleto_1bit_main main_4 (.A(A3), .B(B3), .Cin(1'b0), .S(main_4_s), .Bout(main_4_bout));
  \Decodificador_Binário_para_Algorismo_Decimal_main  main_5 (
    .E8(main_4_s), .E4(main_3_s), .E2(main_2_s), .E1(main_1_s), .M(main_5_m), .TL(main_5_tl), .T(main_5_t),
    .TR(main_5_tr), .BL(main_5_bl), .B(main_5_b), .BR(main_5_br));
  _7_Segment_Display u_7_segment_display_1 (
    .g(main_5_m), .f(main_5_tl), .a(main_5_t), .b(main_5_tr), .e(main_5_bl), .d(main_5_b), .c(main_5_br));  // open: dp
endmodule
